# Fritzing sketch attiny85_fritzing (saved by Fritzing 0.9.3b)
breadboards: 1

parts:
  3V = Battery Holders [package=battcom_20mm_pth]
  U1 = attiny85 [package=dip]
  LED1 = LED - 5mm [color="Red (633nm)" package="5 mm [THT]"]
  R1 = Resistor [tolerance=±5% resistance=47 package=THT]
  Potentiometer = POT [package=pot_alpha_rv16af-20]

nets:
  N1: 3V.+, U1.Pin_8, Potentiometer.A
  N2: 3V.-, U1.Pin_4, R1.Pin_0, Potentiometer.E
  N3: U1.Pin_2, Potentiometer.S
  N4: U1.Pin_5, LED1.anode
  N5: LED1.cathode, R1.Pin_1

notes:
  GND
  VCC
  0
  1
  2
  RESET
  3
  4
