# Fritzing sketch attiny85_rgb_fritzing (saved by Fritzing 0.9.3b)
circuit board: 8.46667cm x 5.64444cm
breadboards: 1

parts:
  3V = Battery Holders [package=battcom_20mm_pth]
  U1 = attiny85 [package=dip]
  Potentiometer = POT [package=pot_alpha_rv16af-20]
  LED1 = RGB LED (com. cathode, rgb) [package="5 mm [THT]"]
  R2 = Resistor [tolerance=±5% resistance=47 package=THT]
  R3 = Resistor [tolerance=±5% resistance=47 package=THT]
  R4 = Resistor [tolerance=±5% resistance=47 package=THT]

nets:
  N1: 3V.+, U1.Pin_8, Potentiometer.A
  N2: 3V.-, U1.Pin_4, Potentiometer.E, LED1.common_cathode
  N3: U1.Pin_2, Potentiometer.S
  N4: U1.Pin_5, R2.Pin_0
  N5: U1.Pin_6, R3.Pin_0
  N6: U1.Pin_7, R4.Pin_0
  N7: LED1.red_anode, R4.Pin_1
  N8: LED1.green_anode, R3.Pin_1
  N9: LED1.blue_anode, R2.Pin_1

notes:
  GND
  VCC
  0
  1
  2
  RESET
  3
  4
